# Fritzing sketch Circuit Diagram (saved by Fritzing 0.9.3b)
breadboards: 1

parts:
  FC-1 = Sound Sensor
  Part1 = Arduino Ethernet Shield (Rev3)
  LCD1 = LCD screen
  R1 = Resistor [tolerance=±5% resistance=220 package=THT]
  LED1 = LED - 5mm [color="Red (633nm)" package="5 mm [THT]"]
  SPKR1 = Loudspeaker  # not connected

nets:
  VCC: FC-1.VCC, Part1.5V, LCD1.VDD, LCD1.LED+
  GND: FC-1.GND, Part1.GND, LCD1.VSS, LCD1.R/W, LCD1.LED-, R1.Pin_0, LED1.cathode
  N1: FC-1.OUT, Part1.A3
  N2: Part1.D8, LCD1.E
  N3: Part1.PWM_D9, LCD1.RS
  N4: Part1.PWM_D11, LED1.anode
  N5: Part1.SDCS, LCD1.DB7
  N6: Part1.PWM_D5, LCD1.DB6
  N7: Part1.PWM_D6, LCD1.DB5
  N8: Part1.D7, LCD1.DB4
  N9: LCD1.V0, R1.Pin_1

notes:
  SOUND MODULE (Microphone) -->
  <--LCD Display
  (16 x 2)
  <-- Arduino UNO
  SPEAKER -->
